// Logisim project stylo.circ as structural Verilog: 10 circuits, main circuit Main
module Main (
);

  wire clock_1_out, controlled_buffer_1_out, isStarted, keyboard_1_avail, Lose, or_1_out, r, start,
       tacktdel_1_out_2, tg, title_1_out_18, up_down_1_out_4;
  wire [3:0] score_1_out_4, \score_1_десятки_мс , \score_1_единицы_сек , \score_1_сотни_мс ;
  wire [6:0] val;
  wire [15:0] right_left_1_out_7, right_left_1_out_9, right_left_1_out_10, up_down_1_out_5, up_down_1_out_6,
       up_down_1_out_7, up_down_1_out_8, up_down_1_out_9, up_down_1_out_10, up_down_1_out_11,
       up_down_1_out_12, up_down_1_out_13, up_down_1_out_14, up_down_1_out_15, up_down_1_out_16,
       up_down_1_out_17, up_down_1_out_18, up_down_1_out_19, up_down_1_out_20, up_down_1_out_21,
       up_down_1_out_22, up_down_1_out_23, up_down_1_out_24, up_down_1_out_25, up_down_1_out_26,
       up_down_1_out_27, up_down_1_out_28, up_down_1_out_29, up_down_1_out_30, up_down_1_out_31,
       up_down_1_out_32, up_down_1_out_33, up_down_1_out_34, up_down_1_out_35, up_down_1_out_36;
  wire [31:0] title_1_out_3, title_1_out_4, title_1_out_5, title_1_out_6, title_1_out_7, title_1_out_8,
       title_1_out_9, title_1_out_10, title_1_out_11, title_1_out_12, title_1_out_13, title_1_out_14,
       title_1_out_15, title_1_out_16, title_1_out_19, title_1_out_20;

  Up_down up_down_1 (
    .out_5(up_down_1_out_5), .out_6(up_down_1_out_6), .out_7(up_down_1_out_7), .out_8(up_down_1_out_8),
    .out_9(up_down_1_out_9), .out_10(up_down_1_out_10), .out_11(up_down_1_out_11), .out_12(up_down_1_out_12),
    .out_13(up_down_1_out_13), .out_14(up_down_1_out_14), .out_15(up_down_1_out_15),
    .out_16(up_down_1_out_16), .out_17(up_down_1_out_17), .out_18(up_down_1_out_18),
    .out_19(up_down_1_out_19), .out_20(up_down_1_out_20), .out_21(up_down_1_out_21),
    .out_22(up_down_1_out_22), .out_23(up_down_1_out_23), .out_24(up_down_1_out_24),
    .out_25(up_down_1_out_25), .out_26(up_down_1_out_26), .out_27(up_down_1_out_27),
    .out_28(up_down_1_out_28), .out_29(up_down_1_out_29), .out_30(up_down_1_out_30),
    .out_31(up_down_1_out_31), .out_32(up_down_1_out_32), .out_33(up_down_1_out_33),
    .out_34(up_down_1_out_34), .out_35(up_down_1_out_35), .out_36(up_down_1_out_36), .in_1(tg), .in_2(val),
    .out_4(up_down_1_out_4), .in_3(r));
  Right_left right_left_1 (
    .in_6(val), .in_5(tg), .out_7(right_left_1_out_7), .in_1(up_down_1_out_34), .out_8(Lose),
    .in_2(up_down_1_out_36), .out_9(right_left_1_out_9), .in_3(up_down_1_out_35),
    .out_10(right_left_1_out_10), .in_4(title_1_out_18));
  assign controlled_buffer_1_out = keyboard_1_avail ? tg : 1'bz;  // Controlled_Buffer controlled_buffer_1
  Hex_Digit_Display hex_digit_display_1 (.value(\score_1_единицы_сек ));  // open: dp
  Hex_Digit_Display hex_digit_display_2 (.value(score_1_out_4));  // open: dp
  DotMatrix #(.inputtype("row"), .matrixcols(16), .matrixrows(32)) dotmatrix_1 (
    .row0(up_down_1_out_5), .row1(up_down_1_out_6), .row2(up_down_1_out_7), .row3(up_down_1_out_8),
    .row4(up_down_1_out_9), .row5(up_down_1_out_10), .row6(up_down_1_out_11), .row7(up_down_1_out_12),
    .row8(up_down_1_out_13), .row9(up_down_1_out_14), .row10(up_down_1_out_15), .row11(up_down_1_out_16),
    .row12(up_down_1_out_17), .row13(up_down_1_out_18), .row14(up_down_1_out_19), .row15(up_down_1_out_20),
    .row16(up_down_1_out_21), .row17(up_down_1_out_22), .row18(up_down_1_out_23), .row19(up_down_1_out_24),
    .row20(up_down_1_out_25), .row21(up_down_1_out_26), .row22(up_down_1_out_27), .row23(up_down_1_out_28),
    .row24(up_down_1_out_29), .row25(up_down_1_out_30), .row26(up_down_1_out_31), .row27(up_down_1_out_32),
    .row28(up_down_1_out_33), .row29(right_left_1_out_7), .row30(right_left_1_out_10),
    .row31(right_left_1_out_9));
  Title title_1 (
    .out_3(title_1_out_3), .out_4(title_1_out_4), .out_5(title_1_out_5), .out_6(title_1_out_6),
    .out_7(title_1_out_7), .out_8(title_1_out_8), .out_9(title_1_out_9), .out_10(title_1_out_10),
    .out_11(title_1_out_11), .out_12(title_1_out_12), .out_13(title_1_out_13), .out_14(title_1_out_14),
    .out_15(title_1_out_15), .out_16(title_1_out_16), .out_19(title_1_out_19), .out_20(title_1_out_20),
    .start(start), .out_17(isStarted), .in_2(Lose), .out_18(title_1_out_18));
  DotMatrix #(.matrixcols(16), .matrixrows(32)) dotmatrix_2 (
    .col0(title_1_out_3), .col1(title_1_out_5), .col2(title_1_out_7), .col3(title_1_out_9),
    .col4(title_1_out_11), .col5(title_1_out_13), .col6(title_1_out_15), .col7(title_1_out_19),
    .col8(title_1_out_4), .col9(title_1_out_6), .col10(title_1_out_8), .col11(title_1_out_10),
    .col12(title_1_out_12), .col13(title_1_out_14), .col14(title_1_out_16), .col15(title_1_out_20));
  Keyboard_part #(.buflen(4)) keyboard_1 (
    .clk(controlled_buffer_1_out), .avail(keyboard_1_avail), .data(val));  // open: re, clr
  Hex_Digit_Display hex_digit_display_3 (.value(\score_1_десятки_мс ));  // open: dp
  Hex_Digit_Display hex_digit_display_4 (.value(\score_1_сотни_мс ));  // open: dp
  Score score_1 (
    .in_1(r), .in_2(start), .in_3(up_down_1_out_4), .\Единицы_сек (\score_1_единицы_сек ),
    .\Сотни_мс (\score_1_сотни_мс ), .\Десятки_мс (\score_1_десятки_мс ), .out_4(score_1_out_4));
  Keyboard keyboard_2 (.in_1(val), .in_2(tg), .out_6(start), .out_7(r));  // open: out_3, out_5, out_4, out_8
  TacktDel tacktdel_1 (.out_2(tacktdel_1_out_2), .in_1(clock_1_out));
  Clock clock_1 (.out(clock_1_out));
  or or_1 (or_1_out, Lose, r);
  and and_1 (tg, or_1_out, tacktdel_1_out_2);

  // Notes on the sheet:
  //   a/d - left/right
  //   r - restart
  //   space - start/pause
  //   w/s - speedUp/down
endmodule

module Right_left (
  input  [15:0] in_1,
  input  [15:0] in_2,
  input  [15:0] in_3,
  input  in_4,
  input  in_5,
  input  [6:0] in_6,
  output [15:0] out_7,
  output out_8,
  output [15:0] out_9,
  output [15:0] out_10
);

  wire and_1_out, and_2_out, and_3_out, collision_1_out_4, collision_2_out_4, collision_3_out_4,
       keyboard_1_out_3, keyboard_1_out_4, not_1_out, or_1_out;
  wire [3:0] counter_1_q;
  wire [15:0] decoder_1_out15;

  and and_1 (and_1_out, keyboard_1_out_4, and_3_out);
  Keyboard keyboard_1 (
    .out_3(keyboard_1_out_3), .in_1(in_6), .out_4(keyboard_1_out_4), .in_2(and_3_out));  // open: out_5, out_6, out_8, out_7
  Decoder #(.select(4)) decoder_1 (
    .out0(decoder_1_out15[15]), .out1(decoder_1_out15[14]), .out2(decoder_1_out15[13]),
    .out3(decoder_1_out15[12]), .out4(decoder_1_out15[11]), .out5(decoder_1_out15[10]),
    .out6(decoder_1_out15[9]), .out7(decoder_1_out15[8]), .out8(decoder_1_out15[7]),
    .out9(decoder_1_out15[6]), .out10(decoder_1_out15[5]), .out11(decoder_1_out15[4]),
    .out12(decoder_1_out15[3]), .out13(decoder_1_out15[2]), .out14(decoder_1_out15[1]),
    .out15(decoder_1_out15[0]), .sel(counter_1_q));  // open: en
  Counter #(.width(4), .max('he), .ongoal("stay")) counter_1 (
    .load(and_1_out), .Q(counter_1_q), .clk(or_1_out));  // open: D, count, carry, clr
  or or_1 (or_1_out, and_1_out, and_2_out);
  and and_2 (and_2_out, keyboard_1_out_3, and_3_out);
  not not_1 (not_1_out, in_4);
  and and_3 (and_3_out, not_1_out, in_5);
  Collision collision_1 (.in_1(in_1), .in_2(decoder_1_out15), .out_3(out_7), .out_4(collision_1_out_4));
  Collision collision_2 (.in_1(in_2), .in_2(decoder_1_out15), .out_3(out_9), .out_4(collision_2_out_4));
  Collision collision_3 (.in_1(in_3), .in_2(decoder_1_out15), .out_3(out_10), .out_4(collision_3_out_4));
  and and_4 (out_8, collision_1_out_4, collision_2_out_4, collision_3_out_4);

  // Other names for the same wires on the sheet: _1 = out_8
endmodule

module Up_down (
  input  in_1,
  input  [6:0] in_2,
  input  in_3,
  output out_4,
  output [15:0] out_5,
  output [15:0] out_6,
  output [15:0] out_7,
  output [15:0] out_8,
  output [15:0] out_9,
  output [15:0] out_10,
  output [15:0] out_11,
  output [15:0] out_12,
  output [15:0] out_13,
  output [15:0] out_14,
  output [15:0] out_15,
  output [15:0] out_16,
  output [15:0] out_17,
  output [15:0] out_18,
  output [15:0] out_19,
  output [15:0] out_20,
  output [15:0] out_21,
  output [15:0] out_22,
  output [15:0] out_23,
  output [15:0] out_24,
  output [15:0] out_25,
  output [15:0] out_26,
  output [15:0] out_27,
  output [15:0] out_28,
  output [15:0] out_29,
  output [15:0] out_30,
  output [15:0] out_31,
  output [15:0] out_32,
  output [15:0] out_33,
  output [15:0] out_34,
  output [15:0] out_35,
  output [15:0] out_36
);

  wire d_ff_1_q, d_ff_2_q, d_ff_3_q, d_ff_4_q, d_ff_5_q, d_ff_6_q, d_ff_6_qn, faster_slower_1_out_3,
       not_1_out, or_1_out;
  wire [7:0] harvard_1_out_3, harvard_1_out_4, register_1_q;
  wire [15:0] multiplexer_1_out, undriven;

  Harvard harvard_1 (.in_1(in_1), .out_3(harvard_1_out_3), .in_2(not_1_out), .out_4(harvard_1_out_4));
  Faster_slower faster_slower_1 (.in_1(in_1), .in_2(in_2), .out_4(out_4), .out_3(faster_slower_1_out_3));
  Register register_1 (.D(harvard_1_out_4), .Q(register_1_q), .clk(not_1_out));  // open: en, clr
  D_Flip_Flop d_ff_1 (.clk(faster_slower_1_out_3), .D(d_ff_6_qn), .Q(d_ff_1_q));  // open: Qn, preset, en, reset
  D_Flip_Flop d_ff_2 (.clk(faster_slower_1_out_3), .D(d_ff_1_q), .Q(d_ff_2_q));  // open: Qn, preset, en, reset
  D_Flip_Flop d_ff_3 (.clk(faster_slower_1_out_3), .D(d_ff_2_q), .Q(d_ff_3_q));  // open: Qn, preset, en, reset
  D_Flip_Flop d_ff_4 (.clk(faster_slower_1_out_3), .D(d_ff_3_q), .Q(d_ff_4_q));  // open: Qn, preset, en, reset
  D_Flip_Flop d_ff_5 (.clk(faster_slower_1_out_3), .D(d_ff_4_q), .Q(d_ff_5_q));  // open: Qn, preset, en, reset
  Multiplexer #(.width(16)) multiplexer_1 (
    .in0({16{1'b0}}),
    .in1({{2{register_1_q[7]}}, {2{register_1_q[6]}}, {2{register_1_q[5]}}, {2{register_1_q[4]}}, {2{register_1_q[3]}}, {2{register_1_q[2]}}, {2{register_1_q[1]}}, {2{register_1_q[0]}}}),
    .out(multiplexer_1_out), .sel(not_1_out));  // open: en
  not not_1 (not_1_out, or_1_out);
  or or_1 (or_1_out, d_ff_4_q, d_ff_5_q, d_ff_6_q);
  D_Flip_Flop d_ff_6 (
    .clk(faster_slower_1_out_3), .D(d_ff_5_q), .Q(d_ff_6_q), .Qn(d_ff_6_qn));  // open: preset, en, reset
  Shift_Register #(.width(16), .length(32)) shift_register_1 (
    .shift(1'b1), .in(multiplexer_1_out), .clk(faster_slower_1_out_3), .load(1'b0), .clr(in_3), .q0(out_5),
    .q1(out_6), .q2(out_7), .q3(out_8), .q4(out_9), .q5(out_10), .q6(out_11), .q7(out_12), .q8(out_13),
    .q9(out_14), .q10(out_15), .q11(out_16), .d12(undriven), .q12(out_17), .d13(undriven), .q13(out_18),
    .q14(out_19), .q15(out_20), .q16(out_21), .q17(out_22), .q18(out_23), .q19(out_24), .q20(out_25),
    .q21(out_26), .q22(out_27), .q23(out_28), .q24(out_29), .q25(out_30), .q26(out_31), .q27(out_32),
    .q28(out_33), .q29(out_34), .q30(out_35), .q31(out_36));  // open: out, d0, d1, d2, d3, d4, d5, d6, d7, d8, d9, d10, d11, d14, d15, d16, d17, d18, d19, d20, d21, d22, d23, d24, d25, d26, d27, d28, d29, d30, d31
endmodule

module Faster_slower (
  input  in_1,
  input  [6:0] in_2,
  output out_3,
  output out_4
);

  wire d_ff_1_q, d_ff_2_q, d_ff_3_q, d_ff_4_q, d_ff_4_qn, d_ff_5_q, d_ff_6_q, d_ff_7_q, d_ff_8_q, d_ff_8_qn,
       d_ff_9_q, d_ff_9_qn, d_ff_10_q, d_ff_10_qn, d_ff_11_q, d_ff_11_qn, keyboard_1_out_6, or_1_out;
  wire [1:0] keyboard_1_out_5;

  D_Flip_Flop d_ff_1 (.clk(in_1), .D(d_ff_2_q), .Q(d_ff_1_q));  // open: Qn, preset, en, reset
  D_Flip_Flop d_ff_2 (.clk(in_1), .D(d_ff_10_qn), .Q(d_ff_2_q));  // open: Qn, preset, en, reset
  D_Flip_Flop d_ff_3 (.clk(in_1), .D(d_ff_8_qn), .Q(d_ff_3_q));  // open: Qn, preset, en, reset
  D_Flip_Flop d_ff_4 (.clk(in_1), .D(or_1_out), .Q(d_ff_4_q), .Qn(d_ff_4_qn));  // open: preset, en, reset
  or or_1 (or_1_out, d_ff_4_qn, d_ff_9_qn);
  D_Flip_Flop d_ff_5 (.clk(in_1), .D(d_ff_1_q), .Q(d_ff_5_q));  // open: Qn, preset, en, reset
  D_Flip_Flop d_ff_6 (.clk(in_1), .D(d_ff_11_qn), .Q(d_ff_6_q));  // open: Qn, preset, en, reset
  D_Flip_Flop d_ff_7 (.clk(in_1), .D(d_ff_6_q), .Q(d_ff_7_q));  // open: Qn, preset, en, reset
  D_Flip_Flop d_ff_8 (.clk(in_1), .D(d_ff_3_q), .Q(d_ff_8_q), .Qn(d_ff_8_qn));  // open: preset, en, reset
  D_Flip_Flop d_ff_9 (.clk(in_1), .D(d_ff_4_q), .Q(d_ff_9_q), .Qn(d_ff_9_qn));  // open: preset, en, reset
  D_Flip_Flop d_ff_10 (.clk(in_1), .D(d_ff_5_q), .Q(d_ff_10_q), .Qn(d_ff_10_qn));  // open: preset, en, reset
  D_Flip_Flop d_ff_11 (.clk(in_1), .D(d_ff_7_q), .Q(d_ff_11_q), .Qn(d_ff_11_qn));  // open: preset, en, reset
  Keyboard keyboard_1 (
    .in_1(in_2), .out_5(keyboard_1_out_5), .in_2(in_1), .out_6(keyboard_1_out_6));  // open: out_3, out_4, out_8, out_7
  Multiplexer #(.select(2)) multiplexer_1 (
    .in0(d_ff_10_q), .in1(d_ff_11_q), .in2(d_ff_8_q), .in3(d_ff_9_q), .out(out_4), .sel(keyboard_1_out_5));  // open: en
  and and_1 (out_3, out_4, keyboard_1_out_6);
endmodule

module Keyboard (
  input  [6:0] in_1,
  input  in_2,
  output out_3,
  output out_4,
  output [1:0] out_5,
  output out_6,
  output out_7,
  output [6:0] out_8
);

  wire comparator_3_eq, comparator_4_eq, comparator_5_eq;

  Comparator #(.width(7)) comparator_1 (.a(in_1), .b(7'b1100100), .eq(out_3));  // open: gt, lt
  Comparator #(.width(7)) comparator_2 (.a(in_1), .b(7'b1100001), .eq(out_4));  // open: gt, lt
  Comparator #(.width(7)) comparator_3 (.a(in_1), .b(7'b1110011), .eq(comparator_3_eq));  // open: gt, lt
  Comparator #(.width(7)) comparator_4 (.a(in_1), .b(7'b1110111), .eq(comparator_4_eq));  // open: gt, lt
  Comparator #(.width(7)) comparator_5 (.a(in_1), .b(7'b0100000), .eq(comparator_5_eq));  // open: gt, lt
  Comparator #(.width(7)) comparator_6 (.a(in_1), .b(7'b1110010), .eq(out_7));  // open: gt, lt
  Counter #(.width(2), .max('h3), .ongoal("stay")) counter_1 (
    .load(comparator_3_eq), .count(comparator_4_eq), .Q(out_5), .clk(in_2));  // open: D, carry, clr
  Counter #(.width(1), .max('h1)) counter_2 (
    .count(comparator_5_eq), .Q(out_6), .clk(in_2));  // open: load, D, carry, clr

  assign out_8 = in_1;

  // Other names for the same wires on the sheet: tg = in_2
endmodule

module Score (
  input  in_1,
  input  in_2,
  input  in_3,
  output [3:0] out_4,
  output [3:0] \Единицы_сек ,
  output [3:0] \Сотни_мс ,
  output [3:0] \Десятки_мс 
);

  wire and_1_out, and_2_out, and_3_out, and_4_out, and_5_out, and_6_out, or_1_out, or_2_out, or_3_out,
       or_4_out, or_5_out;
  wire [3:0] counter_5_q;

  Counter #(.width(4), .max('hf)) counter_1 (
    .Q(out_4), .clk(and_3_out), .clr(or_1_out));  // open: load, D, count, carry
  or or_1 (or_1_out, in_1, and_2_out);
  and and_1 (and_1_out, in_2, in_3);
  Counter #(.width(4), .max('hf)) counter_2 (
    .Q(\Единицы_сек ), .clk(and_4_out), .clr(or_2_out));  // open: load, D, count, carry
  or or_2 (or_2_out, in_1, and_3_out);
  and and_2 (and_2_out, out_4[3], ~out_4[2], out_4[1], ~out_4[0]);  // AND_Gate
  and and_3 (and_3_out, \Единицы_сек [3], ~\Единицы_сек [2], \Единицы_сек [1], ~\Единицы_сек [0]);  // AND_Gate
  Counter #(.width(4), .max('hf)) counter_3 (
    .Q(\Сотни_мс ), .clk(and_5_out), .clr(or_3_out));  // open: load, D, count, carry
  or or_3 (or_3_out, in_1, and_4_out);
  and and_4 (and_4_out, \Сотни_мс [3], ~\Сотни_мс [2], \Сотни_мс [1], ~\Сотни_мс [0]);  // AND_Gate
  Counter #(.width(4), .max('hf)) counter_4 (
    .Q(\Десятки_мс ), .clk(and_6_out), .clr(or_4_out));  // open: load, D, count, carry
  or or_4 (or_4_out, in_1, and_5_out);
  and and_5 (and_5_out, \Десятки_мс [3], ~\Десятки_мс [2], \Десятки_мс [1], ~\Десятки_мс [0]);  // AND_Gate
  Counter #(.width(4), .max('hf)) counter_5 (
    .Q(counter_5_q), .clk(and_1_out), .clr(or_5_out));  // open: load, D, count, carry
  or or_5 (or_5_out, in_1, and_6_out);
  and and_6 (and_6_out, counter_5_q[3], ~counter_5_q[2], counter_5_q[1], ~counter_5_q[0]);  // AND_Gate
endmodule

module Collision (
  input  [15:0] in_1,
  input  [15:0] in_2,
  output [15:0] out_3,
  output out_4
);

  wire and_1_out, and_2_out, and_3_out, and_4_out, and_5_out, and_6_out, and_7_out, and_8_out, and_9_out,
       and_10_out, and_11_out, and_12_out, and_13_out, and_14_out, and_15_out, and_16_out, and_17_out,
       and_18_out, and_19_out, and_20_out, and_21_out, and_22_out, and_23_out, and_24_out, and_25_out,
       and_26_out, and_27_out, and_28_out, and_29_out, and_30_out, and_31_out, and_32_out, or_2_out,
       or_3_out, or_4_out;
  wire [15:0] or_1_out, shifter_1_out;

  assign or_1_out = in_1 | in_2;  // OR_Gate or_1, 16 bits wide
  Adder #(.width(16)) adder_1 (.a(or_1_out), .b(shifter_1_out), .out(out_3));  // open: cin, cout
  Shifter #(.width(16), .shift("lr")) shifter_1 (.in(in_2), .\dist (4'b0001), .out(shifter_1_out));
  and and_1 (and_1_out, in_1[14], in_2[14]);
  and and_2 (and_2_out, in_1[15], in_2[15]);
  and and_3 (and_3_out, in_1[15], shifter_1_out[15]);
  and and_4 (and_4_out, in_1[12], in_2[12]);
  and and_5 (and_5_out, in_1[13], in_2[13]);
  and and_6 (and_6_out, in_1[13], shifter_1_out[13]);
  and and_7 (and_7_out, in_1[14], shifter_1_out[14]);
  and and_8 (and_8_out, in_1[10], in_2[10]);
  and and_9 (and_9_out, in_1[11], in_2[11]);
  and and_10 (and_10_out, in_1[11], shifter_1_out[11]);
  and and_11 (and_11_out, in_1[12], shifter_1_out[12]);
  and and_12 (and_12_out, in_1[9], in_2[9]);
  and and_13 (and_13_out, in_1[9], shifter_1_out[9]);
  and and_14 (and_14_out, in_1[10], shifter_1_out[10]);
  and and_15 (and_15_out, in_1[7], in_2[7]);
  and and_16 (and_16_out, in_1[8], in_2[8]);
  and and_17 (and_17_out, in_1[7], shifter_1_out[7]);
  and and_18 (and_18_out, in_1[8], shifter_1_out[8]);
  and and_19 (and_19_out, in_1[5], in_2[5]);
  and and_20 (and_20_out, in_1[6], in_2[6]);
  and and_21 (and_21_out, in_1[5], shifter_1_out[5]);
  and and_22 (and_22_out, in_1[6], shifter_1_out[6]);
  and and_23 (and_23_out, in_1[3], in_2[3]);
  and and_24 (and_24_out, in_1[4], in_2[4]);
  and and_25 (and_25_out, in_1[4], shifter_1_out[4]);
  and and_26 (and_26_out, in_1[2], in_2[2]);
  and and_27 (and_27_out, in_1[2], shifter_1_out[2]);
  and and_28 (and_28_out, in_1[3], shifter_1_out[3]);
  and and_29 (and_29_out, in_1[0], in_2[0]);
  and and_30 (and_30_out, in_1[1], in_2[1]);
  and and_31 (and_31_out, in_1[1], shifter_1_out[1]);
  or or_2 (or_2_out, and_29_out, and_30_out, and_26_out, and_23_out, and_24_out, and_19_out, and_20_out, and_15_out, and_16_out, and_12_out, and_8_out, and_9_out, and_4_out, and_5_out, and_1_out, and_2_out);
  and and_32 (and_32_out, in_1[0], shifter_1_out[0]);
  or or_3 (or_3_out, and_32_out, and_31_out, and_27_out, and_28_out, and_25_out, and_21_out, and_22_out, and_17_out, and_18_out, and_13_out, and_14_out, and_10_out, and_11_out, and_6_out, and_7_out, and_3_out);
  or or_4 (or_4_out, or_2_out, or_3_out);
  not not_1 (out_4, or_4_out);
endmodule

module Harvard (
  input  in_1,
  input  in_2,
  output [7:0] out_3,
  output [7:0] out_4
);

  wire and_2_out, and_3_out, cdm_8_mark5_1_p5, cdm_8_mark5_1_p6, clr, decoder_1_out0, decoder_1_out1,
       decoder_3_out0, decoder_3_out1, decoder_3_out2, I_O_sel, not_1_out, or_1_out, r, r_w, w;
  wire [7:0] addr, cdm_8_mark5_1_p9, cdm_8_mark5_1_p10, controlled_buffer_3_out, demultiplexer_1_out2,
       io_data, multiplexer_1_out, PC, \rand , reg0, reg1, res;

  and and_1 (I_O_sel, and_2_out, decoder_1_out1);
  and and_2 (and_2_out, addr[4], addr[5], addr[6], addr[7], decoder_1_out1);
  // CdM_8_mark5 cdm_8_mark5_1: pin names not known; wires that end beside it: out_3, in_1, in_2, PC, cdm_8_mark5_1_p5, cdm_8_mark5_1_p6, r_w, addr, cdm_8_mark5_1_p9, cdm_8_mark5_1_p10
  and and_3 (and_3_out, decoder_1_out1, ~and_2_out);  // AND_Gate
  Decoder #(.disabled(0)) decoder_1 (
    .out0(decoder_1_out0), .out1(decoder_1_out1), .sel(cdm_8_mark5_1_p5), .en(cdm_8_mark5_1_p6));
  not not_1 (not_1_out, r_w);
  assign io_data = not_1_out ? cdm_8_mark5_1_p9 : 8'bz;  // Controlled_Buffer controlled_buffer_1
  assign cdm_8_mark5_1_p10 = r_w ? io_data : 8'bz;  // Controlled_Buffer controlled_buffer_2
  Random random_1 (.clk(in_1), .out(\rand ));  // open: next, clr
  RAM ram_1 (.addr(addr), .data(io_data), .sel(and_3_out), .clk(in_1), .ld(r_w), .clr(clr));
  ROM rom_1 (.addr(addr), .data(io_data), .sel(decoder_1_out0));
  Decoder decoder_2 (.out0(r), .out1(w), .sel(r_w), .en(I_O_sel));
  Pull_Resistor pull_resistor_1 (.node(r));
  Pull_Resistor pull_resistor_2 (.node(w));
  or or_1 (or_1_out, r, w);
  Decoder #(.select(4)) decoder_3 (
    .out0(decoder_3_out0), .out1(decoder_3_out1), .out2(decoder_3_out2), .sel(addr[3:0]), .en(or_1_out));  // open: out3, out4, out5, out6, out7, out8, out9, out10, out11, out12, out13, out14, out15
  assign controlled_buffer_3_out = r ? io_data : 8'bz;  // Controlled_Buffer controlled_buffer_3
  Demultiplexer #(.select(4), .width(8)) demultiplexer_1 (
    .out2(demultiplexer_1_out2), .in(controlled_buffer_3_out), .sel(addr[3:0]), .en(r));  // open: out0, out1, out3, out4, out5, out6, out7, out8, out9, out10, out11, out12, out13, out14, out15
  Pull_Resistor pull_resistor_3 (.node(decoder_3_out0));
  Pull_Resistor pull_resistor_4 (.node(decoder_3_out1));
  Pull_Resistor pull_resistor_5 (.node(decoder_3_out2));
  assign res = r ? demultiplexer_1_out2 : 8'bz;  // Controlled_Buffer controlled_buffer_4
  assign io_data = w ? multiplexer_1_out : 8'bz;  // Controlled_Buffer controlled_buffer_5
  Multiplexer #(.select(4), .width(8)) multiplexer_1 (
    .in0(reg0), .in1(reg1), .out(multiplexer_1_out), .sel(addr[3:0]), .en(w));  // open: in2, in3, in4, in5, in6, in7, in8, in9, in10, in11, in12, in13, in14, in15
  Register register_1 (.D(\rand ), .en(decoder_3_out0), .Q(reg0), .clk(in_1));  // open: clr
  Register register_2 (.D(\rand ), .en(decoder_3_out1), .Q(reg1), .clk(in_1));  // open: clr
  Register register_3 (.D(res), .en(decoder_3_out2), .Q(out_4), .clk(in_1));  // open: clr

  // Other names for the same wires on the sheet: IOaddr[3:0] = addr[3:0]; clk = in_1; shift[7:0] = \rand 

  // Notes on the sheet:
  //   contents of rom_1 (hex, n*v repeats v):
  //   c0 c4 d2 f0 ba d0 f1 b0 d0 0 d1 0 d3 0 9 b 9d 47 9e 83 4e d3 f2 ae d6 1 215*0 9
  //   запись в регитсры (st)
  //   чтение из регитров (ld)
endmodule

module TacktDel (
  input  in_1,
  output out_2
);

  Counter #(.width(4), .max('hf)) counter_1 (.carry(out_2), .clk(in_1));  // open: load, D, count, Q, clr
endmodule

module Title (
  input  start,
  input  in_2,
  output [31:0] out_3,
  output [31:0] out_4,
  output [31:0] out_5,
  output [31:0] out_6,
  output [31:0] out_7,
  output [31:0] out_8,
  output [31:0] out_9,
  output [31:0] out_10,
  output [31:0] out_11,
  output [31:0] out_12,
  output [31:0] out_13,
  output [31:0] out_14,
  output [31:0] out_15,
  output [31:0] out_16,
  output out_17,
  output out_18,
  output [31:0] out_19,
  output [31:0] out_20
);

  wire not_1_out, not_2_out;
  wire [31:0] L1, L2, L3, L4, L5, L6, L7, L8, L9, L10, L11, L12, L13, L14, P1, P2, P3, P4, P5, P6, P7, P8,
       P9, P10, P11, P12, P13, P14;

  Multiplexer #(.width(32)) multiplexer_1 (.in0(32'h750d7bc4), .in1(P1), .out(out_5), .sel(out_17));  // open: en
  // Probe on out_5
  // Probe on out_7
  Multiplexer #(.width(32)) multiplexer_2 (.in0(32'h55e50a5e), .in1(P2), .out(out_7), .sel(out_17));  // open: en
  // Probe on out_9
  Multiplexer #(.width(32)) multiplexer_3 (.in0(32'h5d0f0bd4), .in1(P3), .out(out_9), .sel(out_17));  // open: en
  Multiplexer #(.width(32)) multiplexer_4 (.in0(32'h1c), .in1(P4), .out(out_11), .sel(out_17));  // open: en
  // Probe on out_11
  // Probe on out_13
  Multiplexer #(.width(32)) multiplexer_5 (.in0(32'h14), .in1(P5), .out(out_13), .sel(out_17));  // open: en
  // Probe on out_15
  Multiplexer #(.width(32)) multiplexer_6 (.in0(32'he), .in1(P6), .out(out_15), .sel(out_17));  // open: en
  // Probe on out_19
  Multiplexer #(.width(32)) multiplexer_7 (.in0(32'h4), .in1(P7), .out(out_19), .sel(out_17));  // open: en
  Multiplexer #(.width(32)) multiplexer_8 (.in0(32'h10000000), .in1(P8), .out(out_4), .sel(out_17));  // open: en
  Multiplexer #(.width(32)) multiplexer_9 (.in0(32'h38000000), .in1(P9), .out(out_6), .sel(out_17));  // open: en
  Multiplexer #(.width(32)) multiplexer_10 (.in0(32'h50000000), .in1(P10), .out(out_8), .sel(out_17));  // open: en
  Multiplexer #(.width(32)) multiplexer_11 (.in0(32'h70000000), .in1(P11), .out(out_10), .sel(out_17));  // open: en
  Multiplexer #(.width(32)) multiplexer_12 (.in0(32'h53a87bd0), .in1(P12), .out(out_12), .sel(out_17));  // open: en
  Multiplexer #(.width(32)) multiplexer_13 (.in0(32'h7aaf529e), .in1(P13), .out(out_14), .sel(out_17));  // open: en
  Multiplexer #(.width(32)) multiplexer_14 (.in0(32'h12e87b50), .in1(P14), .out(out_16), .sel(out_17));  // open: en
  // Probe on out_4
  // Probe on out_6
  // Probe on out_8
  // Probe on out_10
  // Probe on out_12
  // Probe on out_14
  // Probe on out_16
  Multiplexer #(.width(32)) multiplexer_15 (.in0(L1), .in1({32{1'b0}}), .out(P1), .sel(out_18));  // open: en
  Multiplexer #(.width(32)) multiplexer_16 (.in0(L2), .in1(32'h7c000000), .out(P2), .sel(out_18));  // open: en
  Multiplexer #(.width(32)) multiplexer_17 (.in0(L3), .in1(32'h50000000), .out(P3), .sel(out_18));  // open: en
  Multiplexer #(.width(32)) multiplexer_18 (.in0(L4), .in1(32'h71f00000), .out(P4), .sel(out_18));  // open: en
  Multiplexer #(.width(32)) multiplexer_19 (.in0(L5), .in1(32'h1400000), .out(P5), .sel(out_18));  // open: en
  Multiplexer #(.width(32)) multiplexer_20 (.in0(L6), .in1(32'h1f78000), .out(P6), .sel(out_18));  // open: en
  Multiplexer #(.width(32)) multiplexer_21 (.in0(L7), .in1(32'h4000), .out(P7), .sel(out_18));  // open: en
  // Probe on P1
  // Probe on P2
  // Probe on P3
  // Probe on P4
  // Probe on P5
  // Probe on P6
  // Probe on P7
  // Probe on P8
  Multiplexer #(.width(32)) multiplexer_22 (.in0(L8), .in1(32'h4000), .out(P8), .sel(out_18));  // open: en
  Multiplexer #(.width(32)) multiplexer_23 (.in0(L9), .in1(32'h79d00), .out(P9), .sel(out_18));  // open: en
  // Probe on P9
  // Probe on P10
  Multiplexer #(.width(32)) multiplexer_24 (.in0(L10), .in1(32'h1500), .out(P10), .sel(out_18));  // open: en
  Multiplexer #(.width(32)) multiplexer_25 (.in0(L11), .in1(32'h177c), .out(P11), .sel(out_18));  // open: en
  // Probe on P11
  // Probe on P12
  Multiplexer #(.width(32)) multiplexer_26 (.in0(L12), .in1(32'h54), .out(P12), .sel(out_18));  // open: en
  // Probe on P13
  Multiplexer #(.width(32)) multiplexer_27 (.in0(L13), .in1(32'h54), .out(P13), .sel(out_18));  // open: en
  // Probe on P14
  Multiplexer #(.width(32)) multiplexer_28 (.in0(L14), .in1({32{1'b0}}), .out(P14), .sel(out_18));  // open: en
  // Probe on L1
  Multiplexer #(.width(32)) multiplexer_29 (.in0(32'h7df7c000), .in1({32{1'b0}}), .out(L1), .sel(in_2));  // open: en
  Multiplexer #(.width(32)) multiplexer_30 (.in0(32'h10410000), .in1({32{1'b0}}), .out(L2), .sel(in_2));  // open: en
  // Probe on L2
  // Probe on L3
  Multiplexer #(.width(32)) multiplexer_31 (.in0(32'h7df7c000), .in1({32{1'b0}}), .out(L3), .sel(in_2));  // open: en
  // Probe on L4
  Multiplexer #(.width(32)) multiplexer_32 (.in0({32{1'b0}}), .in1({32{1'b0}}), .out(L4), .sel(in_2));  // open: en
  // Probe on L5
  Multiplexer #(.width(32)) multiplexer_33 (.in0(32'h3cf3c000), .in1({32{1'b0}}), .out(L5), .sel(in_2));  // open: en
  // Probe on L6
  Multiplexer #(.width(32)) multiplexer_34 (.in0(32'h28a28000), .in1({32{1'b0}}), .out(L6), .sel(in_2));  // open: en
  Multiplexer #(.width(32)) multiplexer_35 (.in0(32'h3cf3c000), .in1({32{1'b0}}), .out(L7), .sel(in_2));  // open: en
  // Probe on L7
  // Probe on L8
  Multiplexer #(.width(32)) multiplexer_36 (.in0({32{1'b0}}), .in1({32{1'b0}}), .out(L8), .sel(in_2));  // open: en
  Multiplexer #(.width(32)) multiplexer_37 (.in0({32{1'b0}}), .in1({32{1'b0}}), .out(L9), .sel(in_2));  // open: en
  // Probe on L9
  // Probe on L10
  Multiplexer #(.width(32)) multiplexer_38 (.in0({32{1'b0}}), .in1({32{1'b0}}), .out(L10), .sel(in_2));  // open: en
  // Probe on L11
  Multiplexer #(.width(32)) multiplexer_39 (.in0({32{1'b0}}), .in1({32{1'b0}}), .out(L11), .sel(in_2));  // open: en
  Multiplexer #(.width(32)) multiplexer_40 (.in0(32'h7bdd7de), .in1({32{1'b0}}), .out(L12), .sel(in_2));  // open: en
  // Probe on L12
  Multiplexer #(.width(32)) multiplexer_41 (.in0(32'ha55554), .in1({32{1'b0}}), .out(L13), .sel(in_2));  // open: en
  // Probe on L13
  Multiplexer #(.width(32)) multiplexer_42 (.in0(32'hbd755a), .in1({32{1'b0}}), .out(L14), .sel(in_2));  // open: en
  // Probe on L14
  DotMatrix #(.matrixcols(16), .matrixrows(32)) dotmatrix_1 (
    .col0({32{1'b0}}), .col1(out_5), .col2(out_7), .col3(out_9), .col4(out_11), .col5(out_13), .col6(out_15),
    .col7(out_19), .col8(out_4), .col9(out_6), .col10(out_8), .col11(out_10), .col12(out_12), .col13(out_14),
    .col14(out_16), .col15({32{1'b0}}));
  not not_1 (not_1_out, start);
  not not_2 (not_2_out, not_1_out);
  Counter #(.width(1), .max('h1), .ongoal("stay")) counter_1 (
    .load(not_1_out), .Q(out_17), .clk(not_2_out));  // open: D, count, carry, clr
  DotMatrix #(.matrixcols(16), .matrixrows(32)) dotmatrix_2 (
    .col0({32{1'b0}}), .col1(L1), .col2(L2), .col3(L3), .col4(L4), .col5(L5), .col6(L6), .col7(L7),
    .col8(L8), .col9(L9), .col10(L10), .col11(L11), .col12(L12), .col13(L13), .col14(L14), .col15({32{1'b0}}));
  and and_1 (out_18, out_17, not_1_out);

  assign out_3 = {32{1'b0}};
  assign out_20 = {32{1'b0}};

  // Other names for the same wires on the sheet: _1[31:0] = out_5; _2[31:0] = out_7; _3[31:0] = out_9;
  //   _4[31:0] = out_11; _5[31:0] = out_13; _6[31:0] = out_15; _7[31:0] = out_19; _8[31:0] = out_4; _9[31:0] = out_6;
  //   _10[31:0] = out_8; _11[31:0] = out_10; _12[31:0] = out_12; _13[31:0] = out_14; _14[31:0] = out_16; lose = in_2;
  //   s = out_17; start_t = out_18

  // Notes on the sheet:
  //   Start
  //   Pause
  //   Loss
endmodule
